// Logisim project ax8.circ as structural Verilog: 6 circuits, main circuit main
module main (
);

  wire d_flip_flop_1_nq, d_flip_flop_1_q, dipswitch_5_p1, dipswitch_6_p1, dipswitch_7_p1, dipswitch_8_p1,
       dipswitch_9_p1, dipswitch_10_p1, dipswitch_11_p1, dipswitch_12_p1, dipswitch_13_p1, dipswitch_14_p1,
       full_adder_1_cout, full_adder_1_y, ripple_adder_4_1_cout, ripple_adder_8_1_cout, sr_flip_flop_1_nq,
       sr_flip_flop_1_q;
  wire [3:0] ripple_adder_4_1_y, undriven_2, undriven_4;
  wire [7:0] ripple_adder_8_1_y, undriven, undriven_3;

  // DipSwitch dipswitch_1: pin names not known
  // DipSwitch #(.number(4)) dipswitch_2: pin names not known
  // DipSwitch dipswitch_3: pin names not known
  // DipSwitch #(.number(4)) dipswitch_4: pin names not known
  // DipSwitch #(.number(1)) dipswitch_5: pin names not known; wires that end beside it: dipswitch_5_p1
  // DipSwitch #(.number(1)) dipswitch_6: pin names not known; wires that end beside it: dipswitch_6_p1
  // DipSwitch #(.number(1)) dipswitch_7: pin names not known; wires that end beside it: dipswitch_7_p1
  // DipSwitch #(.number(1)) dipswitch_8: pin names not known; wires that end beside it: dipswitch_8_p1
  // DipSwitch #(.number(1)) dipswitch_9: pin names not known; wires that end beside it: dipswitch_9_p1
  Hex_Digit_Display #(.decimalPoint("false")) hex_digit_display_1 (.value(ripple_adder_8_1_y[7:4]));
  ripple_adder_8 ripple_adder_8_1 (
    .A(undriven), .B(undriven_3), .Cin(dipswitch_7_p1), .Y(ripple_adder_8_1_y), .Cout(ripple_adder_8_1_cout));
  LED led_1 (.in(ripple_adder_8_1_cout));
  ripple_adder_4 ripple_adder_4_1 (
    .A(undriven_2), .B(undriven_4), .Cin(dipswitch_8_p1), .Y(ripple_adder_4_1_y), .Cout(ripple_adder_4_1_cout));
  LED led_2 (.in(ripple_adder_4_1_cout));
  LED led_3 (.in(full_adder_1_y));
  full_adder full_adder_1 (
    .A(dipswitch_5_p1), .B(dipswitch_6_p1), .Cin(dipswitch_9_p1), .Y(full_adder_1_y), .Cout(full_adder_1_cout));
  LED led_4 (.in(full_adder_1_cout));
  Hex_Digit_Display #(.decimalPoint("false")) hex_digit_display_2 (.value(ripple_adder_8_1_y[3:0]));
  Hex_Digit_Display #(.decimalPoint("false")) hex_digit_display_3 (.value(ripple_adder_4_1_y));
  // DipSwitch #(.number(1)) dipswitch_10: pin names not known; wires that end beside it: dipswitch_10_p1
  // DipSwitch #(.number(1)) dipswitch_11: pin names not known; wires that end beside it: dipswitch_11_p1
  // DipSwitch #(.number(1)) dipswitch_12: pin names not known; wires that end beside it: dipswitch_12_p1
  // DipSwitch #(.number(1)) dipswitch_13: pin names not known; wires that end beside it: dipswitch_13_p1
  // DipSwitch #(.number(1)) dipswitch_14: pin names not known; wires that end beside it: dipswitch_14_p1
  LED led_5 (.in(sr_flip_flop_1_q));
  sr_flip_flop sr_flip_flop_1 (
    .R(dipswitch_13_p1), .CLK(dipswitch_11_p1), .S(dipswitch_10_p1), .Q(sr_flip_flop_1_q),
    .NQ(sr_flip_flop_1_nq));
  LED led_6 (.in(sr_flip_flop_1_nq));
  LED led_7 (.in(d_flip_flop_1_q));
  d_flip_flop d_flip_flop_1 (.D(dipswitch_12_p1), .E(dipswitch_14_p1), .Q(d_flip_flop_1_q), .NQ(d_flip_flop_1_nq));
  LED led_8 (.in(d_flip_flop_1_nq));

  // Notes on the sheet:
  //   Test: Ripple Adder with 8-bits
  //   Test: Ripple Adder with 4-bits
  //   Test: Full Adder
  //   Test: SR Flip Flop
  //   Test: D Flip Flop
endmodule

module full_adder (
  input  A,
  input  B,
  input  Cin,
  output Y,
  output Cout
);

  wire and_1_out, and_2_out, xor_1_out;

  xor xor_1 (xor_1_out, A, B);
  and and_1 (and_1_out, xor_1_out, Cin);
  and and_2 (and_2_out, A, B);
  xor xor_2 (Y, xor_1_out, Cin);
  or or_1 (Cout, and_1_out, and_2_out);
endmodule

module ripple_adder_4 (
  input  [3:0] A,
  input  [3:0] B,
  input  Cin,
  output [3:0] Y,
  output Cout
);

  wire full_adder_1_cout, full_adder_2_cout, full_adder_3_cout;

  full_adder full_adder_1 (.A(A[0]), .B(B[0]), .Cin(Cin), .Y(Y[0]), .Cout(full_adder_1_cout));
  full_adder full_adder_2 (.A(A[1]), .B(B[1]), .Cin(full_adder_1_cout), .Y(Y[1]), .Cout(full_adder_2_cout));
  full_adder full_adder_3 (.A(A[2]), .B(B[2]), .Cin(full_adder_2_cout), .Y(Y[2]), .Cout(full_adder_3_cout));
  full_adder full_adder_4 (.A(A[3]), .B(B[3]), .Cin(full_adder_3_cout), .Y(Y[3]), .Cout(Cout));
endmodule

module ripple_adder_8 (
  input  [7:0] A,
  input  [7:0] B,
  input  Cin,
  output [7:0] Y,
  output Cout
);

  wire ripple_adder_4_1_cout;

  ripple_adder_4 ripple_adder_4_1 (.A(A[3:0]), .B(B[3:0]), .Cin(Cin), .Y(Y[3:0]), .Cout(ripple_adder_4_1_cout));
  ripple_adder_4 ripple_adder_4_2 (.A(A[7:4]), .B(B[7:4]), .Cin(ripple_adder_4_1_cout), .Y(Y[7:4]), .Cout(Cout));
endmodule

module sr_flip_flop (
  input  R,
  input  CLK,
  input  S,
  output Q,
  output NQ
);

  wire and_1_out, and_2_out;

  and and_1 (and_1_out, R, CLK);
  and and_2 (and_2_out, CLK, S);
  nor nor_1 (Q, and_1_out, NQ);
  nor nor_2 (NQ, Q, and_2_out);

  // Notes on the sheet:
  //   TODO: Fix propagation delay causing floating output until first reset
endmodule

module d_flip_flop (
  input  D,
  input  E,
  output Q,
  output NQ
);

  wire not_1_out;

  not not_1 (not_1_out, D);
  sr_flip_flop sr_flip_flop_1 (.R(not_1_out), .CLK(E), .S(D), .Q(Q), .NQ(NQ));
endmodule
